// Logisim project ALU.circ as structural Verilog: 2 circuits, main circuit ALU
module ALU (
  input  [3:0] in_1,
  input  [15:0] in_2,
  input  [15:0] in_3,
  input  [3:0] in_4,
  output [15:0] out_5,
  output out_6,
  output out_7
);

  wire [15:0] au_1_out_4, logicunit_1_out_4, main_1_out_4;

  LogicUnit logicunit_1 (.in_3(in_3), .out_4(logicunit_1_out_4), .in_2(in_2), .in_1(in_1[1:0]));
  shifter_main main_1 (.in_1(in_1[1:0]), .in_2(in_2), .in_3(in_4), .out_4(main_1_out_4));
  AU au_1 (.in_1(in_1[1:0]), .in_2(in_2), .in_3(in_3), .out_4(au_1_out_4), .out_5(out_7), .out_6(out_6));
  Multiplexer #(.select(2), .width(16), .enable("false")) multiplexer_1 (
    .in0(au_1_out_4), .in1(logicunit_1_out_4), .in2(main_1_out_4), .out(out_5), .sel(in_1[3:2]));  // open: in3

  // Other names for the same wires on the sheet: operation[1:0] = in_1[1:0]; selector[1:0] = in_1[3:2];
  //   input_1[15:0] = in_2; input_2[15:0] = in_3; output[15:0] = out_5; over_flow = out_7; shift_amount[3:0] = in_4;
  //   zero = out_6
endmodule

module Alu_test_bench (
);

  wire clock_1_out, clock_2_out;
  wire [6:0] counter_1_q;
  wire [7:0] rom_1_data;
  wire [15:0] alu_1_out_5, rom_2_data, rom_3_data;

  Clock clock_1 (.out(clock_1_out));
  Counter #(.width(7), .max('h7f)) counter_1 (
    .count(1'b1), .Q(counter_1_q), .clk(clock_1_out));  // open: load, D, carry, clr
  ROM #(.addrWidth(7)) rom_1 (.addr(counter_1_q), .data(rom_1_data), .sel(1'b1));
  ROM #(.addrWidth(7), .dataWidth(16)) rom_2 (.addr(counter_1_q), .data(rom_2_data), .sel(1'b1));
  ROM #(.addrWidth(7), .dataWidth(16)) rom_3 (.addr(counter_1_q), .data(rom_3_data), .sel(1'b1));
  ALU alu_1 (
    .in_1(rom_1_data[3:0]), .in_2(rom_2_data), .in_3(rom_3_data), .in_4(rom_3_data[3:0]), .out_5(alu_1_out_5));  // open: out_6, out_7
  Clock clock_2 (.out(clock_2_out));
  RAM #(.addrWidth(7), .dataWidth(16)) ram_1 (
    .addr(counter_1_q), .data(alu_1_out_5), .sel(1'b1), .clk(clock_2_out), .ld(1'b0));  // open: clr
  // Pins of 4 and 5 bits meet at rom_1_data[4:0]

  // Notes on the sheet:
  //   contents of rom_2 (hex, n*v repeats v):
  //   6a69 7c71 1a22 a400 3fca dcba 9e ae57 8942 1fdf 158f be6a e6e5 6559 1aff 67a4 1aa1 6f8a bd4 a84d
  //   d2d8 3051 39fc b596 98c8 6304 271f 2a2 c1a6 b678 7344 6dd2 302c a975 9ef6 a097 d1bb 798f f60 6e9e
  //   ceae 6614 caf7 17a1 8e19 2f29 157d 9cd3 c0a2 9860 d6f1 c0bb 9c78 64c5 548c 855b c569 d591 a149 cd4
  //   be1a 4702 ff1a 71ac f3d8 72a5 3800 3d9 45c2 a6f2 e49c 1b88 d615 813e 4115 9d4c 1207 228 1ce5 f388
  //   d366 fe21 ba7a 850d 13a8 d139 2aab f5de 9716 8669 aebf 834e ccd8 b9aa ed4b dbf6 4e5c 7585 bc80 6248
  //   dfea 867b aebc d129 f8eb 7e1e 81f5 e890 c7f3 d78e 5f9b eb15 a3e0 81ba 5074 b1 62ac c2a 1c0 4f6c 85c3
  //   e532 2e3 5302 1114 c2d0 1d3e
endmodule
