// Logisim project Arithmatic Unit.circ as structural Verilog: 2 circuits, main circuit main
module main (
  input  [2:0] in_1,
  input  [15:0] in_2,
  input  [15:0] in_3,
  output [15:0] out_4,
  output out_5,
  output out_6
);

  wire c_0, c_1, c_2, c_3, c_4, c_5, c_6, c_7, c_8, c_9, c_10, c_11, c_12, c_13, c_14, c_15, not_1_out, O_0,
       O_1, O_2, O_3, O_4, O_5, O_6, O_7, O_8, O_9, O_10, O_11, O_12, O_13, O_14, O_15, or_1_out, xor_1_out;
  wire [15:0] bit_extender_1_out, less;

  not not_1 (not_1_out, c_15);
  assign bit_extender_1_out = {{15{1'b0}}, not_1_out};  // Bit_Extender bit_extender_1
  Multiplexer #(.select(2), .width(16), .enable("false")) multiplexer_1 (
    .in0({O_15, O_14, O_13, O_12, O_11, O_10, O_9, O_8, O_7, O_6, O_5, O_4, O_3, O_2, O_1, O_0}), .in1(less),
    .in2(bit_extender_1_out), .out(out_4), .sel(in_1[2:1]));  // open: in3
  xor xor_1 (xor_1_out, O_15, out_5);
  assign less = {{15{1'b0}}, xor_1_out};  // Bit_Extender bit_extender_2
  _1__bit_adder u_1_bit_adder_1 (
    .in_1(in_1[0]), .in_2(in_1[0]), .in_3(in_2[0]), .in_4(in_3[0]), .out_5(O_0), .out_6(c_0));
  _1__bit_adder u_1_bit_adder_2 (.in_1(in_1[0]), .in_2(c_0), .in_3(in_2[1]), .in_4(in_3[1]), .out_5(O_1), .out_6(c_1));
  _1__bit_adder u_1_bit_adder_3 (.in_1(in_1[0]), .in_2(c_1), .in_3(in_2[2]), .in_4(in_3[2]), .out_5(O_2), .out_6(c_2));
  _1__bit_adder u_1_bit_adder_4 (.in_1(in_1[0]), .in_2(c_2), .in_3(in_2[3]), .in_4(in_3[3]), .out_5(O_3), .out_6(c_3));
  _1__bit_adder u_1_bit_adder_5 (.in_1(in_1[0]), .in_2(c_3), .in_3(in_2[4]), .in_4(in_3[4]), .out_5(O_4), .out_6(c_4));
  _1__bit_adder u_1_bit_adder_6 (.in_1(in_1[0]), .in_2(c_4), .in_3(in_2[5]), .in_4(in_3[5]), .out_5(O_5), .out_6(c_5));
  _1__bit_adder u_1_bit_adder_7 (.in_1(in_1[0]), .in_2(c_5), .in_3(in_2[6]), .in_4(in_3[6]), .out_5(O_6), .out_6(c_6));
  _1__bit_adder u_1_bit_adder_8 (.in_1(in_1[0]), .in_2(c_6), .in_3(in_2[7]), .in_4(in_3[7]), .out_5(O_7), .out_6(c_7));
  xor xor_2 (out_5, c_14, c_15);
  or or_1 (or_1_out, O_0, O_1, O_2, O_3, O_4, O_5, O_6, O_7, O_8, O_9, O_10, O_11, O_12, O_13, O_14, O_15);
  not not_2 (out_6, or_1_out);
  _1__bit_adder u_1_bit_adder_9 (.in_1(in_1[0]), .in_2(c_7), .in_3(in_2[8]), .in_4(in_3[8]), .out_5(O_8), .out_6(c_8));
  _1__bit_adder u_1_bit_adder_10 (.in_1(in_1[0]), .in_2(c_8), .in_3(in_2[9]), .in_4(in_3[9]), .out_5(O_9), .out_6(c_9));
  _1__bit_adder u_1_bit_adder_11 (
    .in_1(in_1[0]), .in_2(c_9), .in_3(in_2[10]), .in_4(in_3[10]), .out_5(O_10), .out_6(c_10));
  _1__bit_adder u_1_bit_adder_12 (
    .in_1(in_1[0]), .in_2(c_10), .in_3(in_2[11]), .in_4(in_3[11]), .out_5(O_11), .out_6(c_11));
  _1__bit_adder u_1_bit_adder_13 (
    .in_1(in_1[0]), .in_2(c_11), .in_3(in_2[12]), .in_4(in_3[12]), .out_5(O_12), .out_6(c_12));
  _1__bit_adder u_1_bit_adder_14 (
    .in_1(in_1[0]), .in_2(c_12), .in_3(in_2[13]), .in_4(in_3[13]), .out_5(O_13), .out_6(c_13));
  _1__bit_adder u_1_bit_adder_15 (
    .in_1(in_1[0]), .in_2(c_13), .in_3(in_2[14]), .in_4(in_3[14]), .out_5(O_14), .out_6(c_14));
  _1__bit_adder u_1_bit_adder_16 (
    .in_1(in_1[0]), .in_2(c_14), .in_3(in_2[15]), .in_4(in_3[15]), .out_5(O_15), .out_6(c_15));

  // Other names for the same wires on the sheet: carry_out = c_15; _1__0 = in_2[0]; input_1[15:0] = in_2;
  //   _1__1 = in_2[1]; _1__2 = in_2[2]; _1__3 = in_2[3]; _1__4 = in_2[4]; _1__5 = in_2[5]; _1__6 = in_2[6];
  //   _1__7 = in_2[7]; _1__8 = in_2[8]; _1__9 = in_2[9]; _1__10 = in_2[10]; _1__11 = in_2[11]; _1__12 = in_2[12];
  //   _1__13 = in_2[13]; _1__14 = in_2[14]; _1__15 = in_2[15]; _2__0 = in_3[0]; input_2[15:0] = in_3; _2__1 = in_3[1];
  //   _2__2 = in_3[2]; _2__3 = in_3[3]; _2__4 = in_3[4]; _2__5 = in_3[5]; _2__6 = in_3[6]; _2__7 = in_3[7];
  //   _2__8 = in_3[8]; _2__9 = in_3[9]; _2__10 = in_3[10]; _2__11 = in_3[11]; _2__12 = in_3[12]; _2__13 = in_3[13];
  //   _2__14 = in_3[14]; _2__15 = in_3[15]; Output[15:0] = out_4; over_flow = out_5;
  //   result[15:0] = {O_15, O_14, O_13, O_12, O_11, O_10, O_9, O_8, O_7, O_6, O_5, O_4, O_3, O_2, O_1, O_0};
  //   operation = in_1[0]; selector[2:0] = in_1; zero = out_6
endmodule

module _1__bit_adder (
  input  in_1,
  input  in_2,
  input  in_3,
  input  in_4,
  output out_5,
  output out_6
);

  wire multiplexer_1_out, not_1_out;

  Multiplexer #(.enable("false")) multiplexer_1 (.in0(in_4), .in1(not_1_out), .out(multiplexer_1_out), .sel(in_1));
  not not_1 (not_1_out, in_4);
  Adder #(.width(1)) adder_1 (.a(in_3), .b(multiplexer_1_out), .out(out_5), .cin(in_2), .cout(out_6));

  // Other names for the same wires on the sheet: c_out = out_6; carry_in = in_2; input_1 = in_3; input_2 = in_4;
  //   operation = in_1; output = out_5
endmodule
