// Logisim project Logical unit.circ as structural Verilog: 1 circuit, main circuit LogicUnit
module LogicUnit (
  input  [2:0] in_1,
  input  [15:0] in_2,
  input  [15:0] in_3,
  output [15:0] out_4
);

  wire [15:0] AND, NOR, OR, XOR;

  assign AND = in_2 & in_3;  // AND_Gate and_1, 16 bits wide
  assign OR = in_2 | in_3;  // OR_Gate or_1, 16 bits wide
  assign NOR = ~(in_2 | in_3);  // NOR_Gate nor_1, 16 bits wide
  assign XOR = in_2 ^ in_3;  // XOR_Gate xor_1, 16 bits wide
  Multiplexer #(.select(2), .width(16), .disabled(0), .enable("false")) multiplexer_1 (
    .in0(AND), .in1(OR), .in2(NOR), .in3(XOR), .out(out_4), .sel(in_1[1:0]));

  // Other names for the same wires on the sheet: A[15:0] = in_2; B[15:0] = in_3; OPR[1:0] = in_1[1:0];
  //   OUT[15:0] = out_4
endmodule
