// Logisim project Branch and J Forward.circ as structural Verilog: 5 circuits, main circuit MEM->ID Forward
module Branch_J_Forward (
  input  in_1,
  input  in_2,
  input  in_3,
  input  in_4,
  input  [2:0] in_5,
  input  [2:0] in_6,
  input  [2:0] in_7,
  input  [2:0] in_8,
  input  [2:0] in_9,
  output [1:0] out_10,
  output [1:0] out_11
);

  wire ForwardC_EX, ForwardC_MEM, ForwardC_WB, ForwardD_EX, ForwardD_MEM, ForwardD_WB;

  Calc_FC_FD calc_fc_fd_1 (.EX(ForwardC_EX), .MEM(ForwardC_MEM), .WB(ForwardC_WB), .F1(out_10[1]), .F0(out_10[0]));
  EX__ID_Forward ex_id_forward_1 (
    .in_1(in_1), .in_3(in_5), .in_4(in_8), .in_5(in_9), .out_6(ForwardC_EX), .out_7(ForwardD_EX), .in_2(in_2));
  MEM__ID_Forward mem_id_forward_1 (
    .in_1(in_1), .in_3(in_6), .in_4(in_8), .in_5(in_9), .out_6(ForwardC_MEM), .out_7(ForwardD_MEM),
    .in_2(in_3));
  WB__ID_Forward wb_id_forward_1 (
    .in_1(in_1), .in_3(in_7), .in_4(in_8), .in_5(in_9), .out_6(ForwardC_WB), .out_7(ForwardD_WB), .in_2(in_4));
  Calc_FC_FD calc_fc_fd_2 (.EX(ForwardD_EX), .MEM(ForwardD_MEM), .WB(ForwardD_WB), .F1(out_11[1]), .F0(out_11[0]));

  // Other names for the same wires on the sheet: Branch = in_1; EX_MEM_Rd[2:0] = in_6; ForwardC[1:0] = out_10;
  //   ForwardD[1:0] = out_11; ID_EX_Rd[2:0] = in_5; IF_ID_Rs[2:0] = in_8; IF_ID_Rt[2:0] = in_9; MEM_WB_Rd[2:0] = in_7;
  //   RegWrite_EX = in_2; RegWrite_MEM = in_3; RegWrite_WB = in_4
endmodule

module EX__ID_Forward (
  input  in_1,
  input  in_2,
  input  [2:0] in_3,
  input  [2:0] in_4,
  input  [2:0] in_5,
  output out_6,
  output out_7
);

  wire nR0, Rd__Rs, Rd__Rt;

  and and_1 (out_6, in_1, in_2, nR0, Rd__Rs);
  or or_1 (nR0, in_3[0], in_3[1], in_3[2]);
  Comparator #(.width(3)) comparator_1 (.a(in_3), .b(in_4), .eq(Rd__Rs));  // open: gt, lt
  Comparator #(.width(3)) comparator_2 (.a(in_3), .b(in_5), .eq(Rd__Rt));  // open: gt, lt
  and and_2 (out_7, in_1, in_2, nR0, Rd__Rt);

  // Other names for the same wires on the sheet: Branch = in_1; EX_Rd[2:0] = in_3; ForwardC_EX = out_6;
  //   ForwardD_EX = out_7; ID_Rs[2:0] = in_4; ID_Rt[2:0] = in_5; RegWrite_EX = in_2
endmodule

module MEM__ID_Forward (
  input  in_1,
  input  in_2,
  input  [2:0] in_3,
  input  [2:0] in_4,
  input  [2:0] in_5,
  output out_6,
  output out_7
);

  wire nR0, Rd__Rs, Rd__Rt;

  and and_1 (out_6, in_1, in_2, nR0, Rd__Rs);
  or or_1 (nR0, in_3[0], in_3[1], in_3[2]);
  Comparator #(.width(3)) comparator_1 (.a(in_3), .b(in_4), .eq(Rd__Rs));  // open: gt, lt
  Comparator #(.width(3)) comparator_2 (.a(in_3), .b(in_5), .eq(Rd__Rt));  // open: gt, lt
  and and_2 (out_7, in_1, in_2, nR0, Rd__Rt);

  // Other names for the same wires on the sheet: Branch = in_1; ForwardC_MEM = out_6; ForwardD_MEM = out_7;
  //   ID_Rs[2:0] = in_4; ID_Rt[2:0] = in_5; MEM_Rd[2:0] = in_3; RegWrite_MEM = in_2
endmodule

module WB__ID_Forward (
  input  in_1,
  input  in_2,
  input  [2:0] in_3,
  input  [2:0] in_4,
  input  [2:0] in_5,
  output out_6,
  output out_7
);

  wire nR0, Rd__Rs, Rd__Rt;

  and and_1 (out_6, in_1, in_2, nR0, Rd__Rs);
  or or_1 (nR0, in_3[0], in_3[1], in_3[2]);
  Comparator #(.width(3)) comparator_1 (.a(in_3), .b(in_4), .eq(Rd__Rs));  // open: gt, lt
  Comparator #(.width(3)) comparator_2 (.a(in_3), .b(in_5), .eq(Rd__Rt));  // open: gt, lt
  and and_2 (out_7, in_1, in_2, nR0, Rd__Rt);

  // Other names for the same wires on the sheet: Branch = in_1; ForwardC_WB = out_6; ForwardD_WB = out_7;
  //   ID_Rs[2:0] = in_4; ID_Rt[2:0] = in_5; RegWrite_WB = in_2; WB_Rd[2:0] = in_3
endmodule

module Calc_FC_FD (
  input  EX,
  input  MEM,
  input  WB,
  output F1,
  output F0
);

  wire and_1_out, and_2_out, and_3_out, not_1_out, not_2_out, not_3_out;

  not not_1 (not_1_out, EX);
  not not_2 (not_2_out, EX);
  not not_3 (not_3_out, MEM);
  and and_1 (and_1_out, not_1_out, WB);
  and and_2 (and_2_out, not_2_out, MEM);
  and and_3 (and_3_out, not_3_out, WB);
  or or_1 (F1, and_1_out, and_2_out);
  or or_2 (F0, and_3_out, EX);
endmodule
