// Logisim project ID Branch Forward.circ as structural Verilog: 1 circuit, main circuit ID Branch Forward
module ID_Branch_Forward (
  input  in_1,
  input  [2:0] in_2,
  input  [2:0] in_3,
  input  [2:0] in_4,
  output out_5,
  output out_6
);

  wire nR0, Rd__Rs, Rd__Rt;

  and and_1 (out_5, in_1, nR0, Rd__Rs);
  or or_1 (nR0, in_2[0], in_2[1], in_2[2]);
  Comparator #(.width(3)) comparator_1 (.a(in_2), .b(in_3), .eq(Rd__Rs));  // open: gt, lt
  Comparator #(.width(3)) comparator_2 (.a(in_2), .b(in_4), .eq(Rd__Rt));  // open: gt, lt
  and and_2 (out_6, in_1, nR0, Rd__Rt);

  // Other names for the same wires on the sheet: Branch = in_1; EX_MEM_Rd[2:0] = in_2; ForwardC = out_5;
  //   ForwardD = out_6; IF_ID_Rs[2:0] = in_3; IF_ID_Rt[2:0] = in_4
endmodule
