// Logisim project Full Circuit.circ as structural Verilog: 1 circuit, main circuit Full Circuit
module Full_Circuit (
);

  wire ALUsrc_Ex, ALUsrc_Id, CLK, Ext_Control_Ex, Ext_Control_Id, forwarding_unit_1_out_9, MemRead_Ex,
       MemRead_Id, MemRead_Mem, MemWrite_Ex, MemWrite_Id, MemWrite_Mem, multiplexer_2_out, multiplexer_3_out,
       not_1_out, Overflow, RegWrite_Ex, RegWrite_Id, RegWrite_Mem, RegWrite_Wb, stall, zero;
  wire [1:0] F_Id, F_If, Forward_A, Forward_B, MemToReg_Ex, MemToReg_Id, MemToReg_Mem, MemToReg_Wb, RegDst_Id;
  wire [2:0] multiplexer_1_out, Rd_Ex, Rd_Id, Rd_If, Rd_Mem, Rd_Wb, Rs_Ex, Rs_Id, Rs_If, Rs_Mem, Rt_Ex,
       Rt_Id, Rt_If, Rt_Mem;
  wire [3:0] ALUop_Ex, ALUop_Id, PCsrc_Id, Shift_Amount_Ex, Shift_Amount_Id, Shift_Amount_If;
  wire [4:0] Imm_5_Id, Imm_5_If, OP_Id, OP_If;
  wire [10:0] Imm_11_Id, Imm_11_If;
  wire [15:0] ALU_out_Ex, ALU_out_Mem, ALU_out_Wb, bit_extender_1_out, Ext_Out_Ex, Ext_Out_Id, Imm_11__5_Ex,
       Imm_11__5_Id, Imm_11__5_Mem, Imm_11__5_Wb, ins_Id, ins_If, Mem_out_Mem, Mem_out_Wb, Mem_out_Wb_t,
       multiplexer_4_out, multiplexer_5_out, multiplexer_6_out, multiplexer_7_out, Next_PC, PC_1_Wb, PC_Ex,
       PC_Id, PC_If, PC_Mem, PC_Wb, R1, R2, R3, R4, R5, R6, R7, Rs_Data_Ex, Rs_Data_Id, Rs_Data_Mem,
       Rt_Data_Ex, Rt_Data_Id, Rt_Data_Mem, Write_Data;

  not not_1 (not_1_out, stall);
  // Probe on R1
  Clock clock_1 (.out(CLK));
  // Probe on R2
  // Probe on PC_If
  // Probe on ins_If
  Register #(.width(16)) PC (.D(Next_PC), .en(not_1_out), .Q(PC_If), .clk(CLK));  // open: clr
  // Probe on R3
  // Probe on R4
  // Probe on R5
  InstructionMemory_main main_1 (
    .PC_Address(PC_If), .out_2(Rt_If), .out_3(Rs_If), .out_5(Rd_If), .out_6(F_If), .out_7(OP_If),
    .out_8(Imm_5_If), .out_10(Imm_11_If), .out_9(Shift_Amount_If), .out_4(ins_If));
  // Probe on R6
  // Probe on R7
  Reg_If_Id reg_if_id_1 (
    .in_2(PC_If), .in_3(F_If), .in_4(Rt_If), .in_5(OP_If), .in_6(Rs_If), .in_7(Imm_5_If), .in_8(Rd_If),
    .in_9(Imm_11_If), .in_10(Shift_Amount_If), .in_11(ins_If), .out_12(PC_Id), .out_13(F_Id), .out_14(Rt_Id),
    .out_15(OP_Id), .out_16(Rs_Id), .out_17(Imm_5_Id), .out_18(Rd_Id), .out_19(Imm_11_Id),
    .out_20(Shift_Amount_Id), .out_21(ins_Id), .in_1(CLK));
  Control_Unit control_unit_1 (
    .in_1(OP_Id), .in_2(F_Id), .out_4(ALUsrc_Id), .out_3(ALUop_Id), .out_5(MemRead_Id), .out_6(MemWrite_Id),
    .out_7(Ext_Control_Id), .out_8(MemToReg_Id), .out_9(RegWrite_Id), .out_10(RegDst_Id), .out_11(PCsrc_Id));
  Multiplexer #(.select(2), .width(3), .enable("false")) multiplexer_1 (
    .in0(Rt_Id), .in1(Rd_Id), .in2(3'b001), .in3(3'b111), .out(multiplexer_1_out), .sel(RegDst_Id));
  Hazard_Detection_Unit hazard_detection_unit_1 (
    .in_1(Rs_Id), .in_2(Rt_Id), .in_3(Rt_Ex), .in_4(MemRead_Ex), .out_5(stall));
  RegFile regfile_1 (
    .out_7(Rs_Data_Id), .in_2(Rs_Id), .in_6(CLK), .out_8(Rt_Data_Id), .in_3(Rt_Id), .in_5(RegWrite_Id),
    .in_4(multiplexer_1_out), .in_1(Write_Data), .out_9(R1), .out_10(R2), .out_11(R3), .out_12(R4),
    .out_13(R5), .out_14(R6), .out_15(R7));
  PC_control pc_control_1 (
    .in_1(PC_Id), .in_2(PCsrc_Id), .in_5(Imm_11_Id), .in_6(Imm_5_Id), .out_7(Next_PC), .in_3(Rs_Data_Id),
    .in_4(Rs_Data_Id));  // open: out_8
  assign bit_extender_1_out = {{5{1'b0}}, Imm_11_Id};  // Bit_Extender bit_extender_1
  Extender extender_1 (.in_1(Ext_Control_Id), .in_2(Imm_5_Id), .out_3(Ext_Out_Id));
  Shifter #(.width(16)) shifter_1 (.in(bit_extender_1_out), .\dist (4'b0101), .out(Imm_11__5_Id));
  Multiplexer #(.enable("false")) multiplexer_2 (.in0(RegWrite_Id), .in1(1'b0), .out(multiplexer_2_out), .sel(stall));
  Multiplexer #(.enable("false")) multiplexer_3 (.in0(MemWrite_Id), .in1(1'b0), .out(multiplexer_3_out), .sel(stall));
  Reg_Id_Ex reg_id_ex_1 (
    .in_3(ALUop_Id), .in_4(ALUsrc_Id), .in_5(MemRead_Id), .in_6(multiplexer_3_out), .in_7(Ext_Control_Id),
    .in_8(MemToReg_Id), .in_9(Rs_Data_Id), .in_10(Rt_Data_Id), .out_19(ALUop_Ex), .out_20(ALUsrc_Ex),
    .out_21(MemRead_Ex), .out_22(MemWrite_Ex), .out_23(Ext_Control_Ex), .out_24(MemToReg_Ex),
    .out_25(Rs_Data_Ex), .out_26(Rt_Data_Ex), .in_1(CLK), .in_15(Rs_Id), .out_31(Rs_Ex), .in_16(Rt_Id),
    .out_32(Rt_Ex), .in_17(Rd_Id), .out_33(Rd_Ex), .in_14(multiplexer_2_out), .out_30(RegWrite_Ex),
    .in_12(Ext_Out_Id), .out_28(Ext_Out_Ex), .in_11(Shift_Amount_Id), .out_27(Shift_Amount_Ex),
    .in_13(Imm_11__5_Id), .out_29(Imm_11__5_Ex), .in_2(PC_Id), .out_18(PC_Ex));
  Multiplexer #(.select(2), .width(16), .enable("false")) multiplexer_4 (
    .in0(Rt_Data_Ex), .in1(ALU_out_Wb), .in2(ALU_out_Mem), .out(multiplexer_4_out), .sel(Forward_B));  // open: in3
  Multiplexer #(.select(2), .width(16), .enable("false")) multiplexer_5 (
    .in0(Rs_Data_Ex), .in1(ALU_out_Wb), .in2(ALU_out_Mem), .out(multiplexer_5_out), .sel(Forward_A));  // open: in3
  Multiplexer #(.width(16), .enable("false")) multiplexer_6 (
    .in0(multiplexer_4_out), .in1(Ext_Out_Ex), .out(multiplexer_6_out), .sel(ALUsrc_Ex));
  ALU alu_1 (
    .in_1(ALUop_Ex), .in_2(multiplexer_5_out), .in_3(multiplexer_6_out), .in_4(Shift_Amount_Ex),
    .out_5(ALU_out_Ex), .out_6(zero), .out_7(Overflow));
  Forwarding_Unit forwarding_unit_1 (
    .in_1(Rs_Ex), .in_2(Rt_Ex), .in_3(RegWrite_Mem), .in_4(Rd_Mem), .in_5(RegWrite_Wb), .in_6(Rd_Wb),
    .out_7(Forward_A), .out_8(Forward_B), .out_9(forwarding_unit_1_out_9));
  Multiplexer #(.width(16), .enable("false")) multiplexer_7 (
    .in0(Rt_Data_Ex), .in1(ALU_out_Mem), .out(multiplexer_7_out), .sel(forwarding_unit_1_out_9));
  Reg_Ex_Mem reg_ex_mem_1 (
    .in_1(CLK), .in_2(MemRead_Ex), .in_3(MemWrite_Ex), .in_4(multiplexer_7_out), .in_5(MemToReg_Ex),
    .in_6(Rs_Data_Ex), .in_8(RegWrite_Ex), .in_9(Rs_Ex), .in_10(Rt_Ex), .in_11(Rd_Ex), .out_14(MemRead_Mem),
    .out_15(MemWrite_Mem), .out_16(Rt_Data_Mem), .out_17(MemToReg_Mem), .out_18(Rs_Data_Mem),
    .out_20(RegWrite_Mem), .out_21(Rs_Mem), .out_22(Rt_Mem), .out_23(Rd_Mem), .in_7(ALU_out_Ex),
    .out_19(ALU_out_Mem), .in_12(PC_Ex), .out_24(PC_Mem), .in_13(Imm_11__5_Ex), .out_25(Imm_11__5_Mem));
  Data_Memory data_memory_1 (
    .Address(ALU_out_Mem), .Data_In(Rt_Data_Mem), .MemWrite(MemWrite_Mem), .MemRead(MemRead_Mem), .CLK(CLK),
    .Data_Out(Mem_out_Mem));
  Reg_Mem_Wb reg_mem_wb_1 (
    .in_2(MemToReg_Mem), .in_3(ALU_out_Mem), .in_4(PC_Mem), .in_5(Imm_11__5_Mem), .in_6(Mem_out_Mem),
    .out_9(MemToReg_Wb), .out_10(ALU_out_Wb), .out_11(PC_Wb), .out_12(Imm_11__5_Wb), .out_13(Mem_out_Wb),
    .in_7(RegWrite_Mem), .out_14(RegWrite_Wb), .in_8(Rd_Mem), .out_15(Rd_Wb));  // open: in_1
  Multiplexer #(.select(2), .width(16), .enable("false")) multiplexer_8 (
    .in0(ALU_out_Wb), .in1(Mem_out_Wb_t), .in2(Imm_11__5_Wb), .in3(PC_1_Wb), .out(Write_Data),
    .sel(MemToReg_Wb));
endmodule
