// Logisim project Branch control.circ as structural Verilog: 1 circuit, main circuit Branch Control
module Branch_Control (
  input  [15:0] in_1,
  input  in_2,
  input  in_3,
  input  [15:0] in_4,
  input  [1:0] in_5,
  output [15:0] out_6
);

  wire not_1_out, not_2_out;
  wire [15:0] multiplexer_1_out, multiplexer_2_out, multiplexer_3_out, multiplexer_4_out, Pc___1, Pc___imm;

  Adder #(.width(16)) adder_1 (.a(in_1), .b(16'h1), .out(Pc___1));  // open: cin, cout
  Adder #(.width(16)) adder_2 (.a(in_1), .b(in_4), .out(Pc___imm));  // open: cin, cout
  not not_1 (not_1_out, in_2);
  not not_2 (not_2_out, in_3);
  Multiplexer #(.width(16), .enable("false")) multiplexer_1 (
    .in0(Pc___1), .in1(Pc___imm), .out(multiplexer_1_out), .sel(in_2));
  Multiplexer #(.width(16), .enable("false")) multiplexer_2 (
    .in0(Pc___1), .in1(Pc___imm), .out(multiplexer_2_out), .sel(not_1_out));
  Multiplexer #(.width(16), .enable("false")) multiplexer_3 (
    .in0(Pc___1), .in1(Pc___imm), .out(multiplexer_3_out), .sel(in_3));
  Multiplexer #(.width(16), .enable("false")) multiplexer_4 (
    .in0(Pc___1), .in1(Pc___imm), .out(multiplexer_4_out), .sel(not_2_out));
  Multiplexer #(.select(2), .width(16), .enable("false")) multiplexer_5 (
    .in0(multiplexer_1_out), .in1(multiplexer_2_out), .in2(multiplexer_3_out), .in3(multiplexer_4_out),
    .out(out_6), .sel(in_5));

  // Other names for the same wires on the sheet: Branch_Op[1:0] = in_5; Current_PC[15:0] = in_1;
  //   Immi_Value[15:0] = in_4; Next_PC[15:0] = out_6; SLT_Flag = in_3; Zero_Flag = in_2
endmodule
