// Logisim project Piplining Registers.circ as structural Verilog: 2 circuits, main circuit Reg If/Id
module Reg_If_Id (
  input  in_1,
  input  [15:0] in_2,
  input  [1:0] in_3,
  input  [2:0] in_4,
  input  [4:0] in_5,
  input  [2:0] in_6,
  input  [4:0] in_7,
  input  [2:0] in_8,
  input  [10:0] in_9,
  input  [3:0] in_10,
  input  [15:0] in_11,
  output [15:0] out_12,
  output [1:0] out_13,
  output [2:0] out_14,
  output [4:0] out_15,
  output [2:0] out_16,
  output [4:0] out_17,
  output [2:0] out_18,
  output [10:0] out_19,
  output [3:0] out_20,
  output [15:0] out_21
);

  Register #(.width(16)) Pc_1 (.D(in_2), .Q(out_12), .clk(in_1));  // open: en, clr
  Register #(.width(3)) Rt (.D(in_4), .Q(out_14), .clk(in_1));  // open: en, clr
  Register #(.width(3)) Rs (.D(in_6), .Q(out_16), .clk(in_1));  // open: en, clr
  Register #(.width(3)) Rd (.D(in_8), .Q(out_18), .clk(in_1));  // open: en, clr
  Register #(.width(4)) Shift_amount (.D(in_10), .Q(out_20), .clk(in_1));  // open: en, clr
  Register #(.width(2)) F (.D(in_3), .Q(out_13), .clk(in_1));  // open: en, clr
  Register #(.width(5)) OP (.D(in_5), .Q(out_15), .clk(in_1));  // open: en, clr
  Register #(.width(5)) Imm_5 (.D(in_7), .Q(out_17), .clk(in_1));  // open: en, clr
  Register #(.width(11)) Imm_11 (.D(in_9), .Q(out_19), .clk(in_1));  // open: en, clr
  Register #(.width(16)) Ins (.D(in_11), .Q(out_21), .clk(in_1));  // open: en, clr

  // Other names for the same wires on the sheet: CLK = in_1
endmodule

module Reg_Id_Ex (
  input  in_1,
  input  [3:0] in_2,
  input  in_3,
  input  in_4,
  input  in_5,
  input  in_6,
  input  [1:0] in_7,
  input  [15:0] in_8,
  input  [15:0] in_9,
  input  [3:0] in_10,
  input  [15:0] in_11,
  input  [15:0] in_12,
  input  in_13,
  input  [2:0] in_14,
  input  [2:0] in_15,
  input  [2:0] in_16,
  output [3:0] out_17,
  output out_18,
  output out_19,
  output out_20,
  output out_21,
  output [1:0] out_22,
  output [15:0] out_23,
  output [15:0] out_24,
  output [3:0] out_25,
  output [15:0] out_26,
  output [15:0] out_27,
  output out_28,
  output [2:0] out_29,
  output [2:0] out_30,
  output [2:0] out_31
);

  Register #(.width(4)) ALUop (.D(in_2), .Q(out_17), .clk(in_1));  // open: en, clr
  Register #(.width(1)) MemRead (.D(in_4), .Q(out_19), .clk(in_1));  // open: en, clr
  Register #(.width(1)) Ext_Control (.D(in_6), .Q(out_21), .clk(in_1));  // open: en, clr
  Register #(.width(16)) Rs_Data (.D(in_8), .Q(out_23), .clk(in_1));  // open: en, clr
  Register #(.width(4)) Shift_Amount (.D(in_10), .Q(out_25), .clk(in_1));  // open: en, clr
  Register #(.width(1)) RegWrite (.D(in_13), .Q(out_28), .clk(in_1));  // open: en, clr
  Register #(.width(3)) Rt (.D(in_15), .Q(out_30), .clk(in_1));  // open: en, clr
  Register #(.width(1)) ALUsrc (.D(in_3), .Q(out_18), .clk(in_1));  // open: en, clr
  Register #(.width(1)) MemWrite (.D(in_5), .Q(out_20), .clk(in_1));  // open: en, clr
  Register #(.width(2)) MemToReg (.D(in_7), .Q(out_22), .clk(in_1));  // open: en, clr
  Register #(.width(16)) Rt_Data (.D(in_9), .Q(out_24), .clk(in_1));  // open: en, clr
  Register #(.width(16)) Ex_Out (.D(in_11), .Q(out_26), .clk(in_1));  // open: en, clr
  Register #(.width(16)) Imm_11__5_Id (.D(in_12), .Q(out_27), .clk(in_1));  // open: en, clr
  Register #(.width(3)) Rs (.D(in_14), .Q(out_29), .clk(in_1));  // open: en, clr
  Register #(.width(3)) Rd (.D(in_16), .Q(out_31), .clk(in_1));  // open: en, clr

  // Other names for the same wires on the sheet: CLK = in_1
endmodule
