// Logisim project RegisterFile.circ as structural Verilog: 3 circuits, main circuit SubReg
module SubReg (
  input  in_1,
  input  in_2,
  input  in_3,
  input  [15:0] in_4,
  output [15:0] out_5
);

  wire and_1_out;

  and and_1 (and_1_out, in_2, in_3);
  Register #(.width(16)) register_1 (.D(in_4), .en(and_1_out), .Q(out_5), .clk(in_1), .clr(1'b0));

  // Other names for the same wires on the sheet: CLK = in_1; ReadReg[15:0] = out_5; RegEn = in_2; RegWrite = in_3;
  //   WriteData[15:0] = in_4
endmodule

module RegSelector (
  input  [2:0] in_1,
  input  [15:0] in_2,
  input  [15:0] in_3,
  input  [15:0] in_4,
  input  [15:0] in_5,
  input  [15:0] in_6,
  input  [15:0] in_7,
  input  [15:0] in_8,
  output [15:0] out_9
);

  Multiplexer #(.select(3), .width(16)) multiplexer_1 (
    .in0({16{1'b0}}), .in1(in_2), .in2(in_4), .in3(in_6), .in4(in_8), .in5(in_3), .in6(in_5), .in7(in_7),
    .out(out_9), .sel(in_1));  // open: en

  // Other names for the same wires on the sheet: R1[15:0] = in_2; R2[15:0] = in_4; R3[15:0] = in_6; R4[15:0] = in_8;
  //   R5[15:0] = in_3; R6[15:0] = in_5; R7[15:0] = in_7; ReadData[15:0] = out_9; ReadReg[2:0] = in_1
endmodule

module RegFile (
  input  [15:0] in_1,
  input  [2:0] in_2,
  input  [2:0] in_3,
  input  [2:0] in_4,
  input  in_5,
  input  in_6,
  output [15:0] out_7,
  output [15:0] out_8
);

  wire S1, S2, S3, S4, S5, S6, S7;
  wire [15:0] R1, R2, R3, R4, R5, R6, R7;

  SubReg subreg_1 (.in_1(in_6), .in_2(S1), .in_3(in_5), .in_4(in_1), .out_5(R1));
  SubReg subreg_2 (.in_1(in_6), .in_2(S2), .in_3(in_5), .in_4(in_1), .out_5(R2));
  RegSelector regselector_1 (
    .in_1(in_2), .in_2(R1), .in_4(R2), .in_6(R3), .in_8(R4), .in_3(R5), .in_5(R6), .in_7(R7), .out_9(out_7));
  SubReg subreg_3 (.in_1(in_6), .in_2(S3), .in_3(in_5), .in_4(in_1), .out_5(R3));
  SubReg subreg_4 (.in_1(in_6), .in_2(S4), .in_3(in_5), .in_4(in_1), .out_5(R4));
  Decoder #(.select(3), .enable("false")) decoder_1 (
    .out1(S1), .out2(S2), .out3(S3), .out4(S4), .out5(S5), .out6(S6), .out7(S7), .sel(in_4));  // open: out0
  RegSelector regselector_2 (
    .in_1(in_3), .in_2(R1), .in_4(R2), .in_6(R3), .in_8(R4), .in_3(R5), .in_5(R6), .in_7(R7), .out_9(out_8));
  SubReg subreg_5 (.in_1(in_6), .in_2(S5), .in_3(in_5), .in_4(in_1), .out_5(R5));
  SubReg subreg_6 (.in_1(in_6), .in_2(S6), .in_3(in_5), .in_4(in_1), .out_5(R6));
  SubReg subreg_7 (.in_1(in_6), .in_2(S7), .in_3(in_5), .in_4(in_1), .out_5(R7));

  // Other names for the same wires on the sheet: BusA[15:0] = out_7; BusB[15:0] = out_8; BusW[15:0] = in_1;
  //   CLK = in_6; RA[2:0] = in_2; RB[2:0] = in_3; RegWrite = in_5; RW[2:0] = in_4
endmodule
