// Logisim project SingleCycleRISCmips.circ as structural Verilog: 1 circuit, main circuit Single Cycle circuit
module Single_Cycle_circuit (
);

  wire ALUsrc, CLK, Ext_Control, MemRead, MemWrite, Overflow, RegWrite, zero;
  wire [1:0] F, MemToReg, RegDst;
  wire [2:0] multiplexer_1_out, Rd, Rs, Rt;
  wire [3:0] ALUop, PCsrc, Shift_amount;
  wire [4:0] Imm_5, Imm_5_t, OP;
  wire [10:0] Imm_11, Imm_11_t;
  wire [15:0] ALU_out, bit_extender_1_out, Ext_Out, Imm_11__5, Mem_out, multiplexer_2_out, multiplexer_3_out,
       PC_1, pc_contol_1_p1, pc_contol_1_p7, Rs_Data, Rt_Data;

  Clock clock_1 (.out(CLK));
  // PC_contol pc_contol_1: pin names not known; wires that end beside it: pc_contol_1_p1, zero, ALU_out, Imm_11, Imm_5, PCsrc, pc_contol_1_p7
  Register #(.width(16)) PC (.D(pc_contol_1_p7), .en(1'b1), .Q(pc_contol_1_p1), .clk(CLK));  // open: clr
  Control_Unit control_unit_1 (
    .in_1(OP), .in_2(F), .out_4(ALUsrc), .out_3(ALUop), .out_5(MemRead), .out_6(MemWrite),
    .out_7(Ext_Control), .out_8(MemToReg), .out_9(RegWrite), .out_10(RegDst), .out_11(PCsrc));
  // InstructionMemory_main main_1: pin names not known; wires that end beside it: pc_contol_1_p1, Rt, Rs, Rd, F, OP, Imm_5_t, Shift_amount, Imm_11_t
  Multiplexer #(.select(2), .width(3), .enable("false")) multiplexer_1 (
    .in0(Rt), .in1(Rd), .in2(3'b001), .in3(3'b111), .out(multiplexer_1_out), .sel(RegDst));
  Multiplexer #(.select(2), .width(16), .enable("false")) multiplexer_2 (
    .in0(ALU_out), .in1(Mem_out), .in2(Imm_11__5), .in3(PC_1), .out(multiplexer_2_out), .sel(MemToReg));
  // RegFile regfile_1: pin names not known; wires that end beside it: Rs, Rt, multiplexer_1_out, multiplexer_2_out, RegWrite, CLK, Rs_Data, Rt_Data
  Multiplexer #(.width(16), .enable("false")) multiplexer_3 (
    .in0(Rt_Data), .in1(Ext_Out), .out(multiplexer_3_out), .sel(ALUsrc));
  assign bit_extender_1_out = {{5{1'b0}}, Imm_11_t};  // Bit_Extender bit_extender_1
  Shifter #(.width(16)) shifter_1 (.in(bit_extender_1_out), .\dist (4'b0101), .out(Imm_11__5));
  // ALU alu_1: pin names not known; wires that end beside it: Rs_Data, multiplexer_3_out, Shift_amount, ALUop, zero, ALU_out, Overflow
  Extender extender_1 (.in_1(Ext_Control), .in_2(Imm_5_t), .out_3(Ext_Out));
  Data_Memory data_memory_1 (
    .Address(ALU_out), .Data_In(Rt_Data), .MemWrite(MemWrite), .MemRead(MemRead), .CLK(CLK),
    .Data_Out(Mem_out));
endmodule
