// Logisim project InstructionMemory.circ as structural Verilog: 1 circuit, main circuit main
module main (
  input  [15:0] PC_Address,
  output [2:0] out_2,
  output [2:0] out_3,
  output [2:0] out_4,
  output [1:0] out_5,
  output [4:0] out_6,
  output [4:0] out_7,
  output [3:0] out_8,
  output [10:0] out_9
);

  ROM #(.addrWidth(16), .dataWidth(16)) rom_1 (
    .addr(PC_Address), .data({out_6, out_5, out_4, out_3, out_2}), .sel(1'b1));

  assign out_7 = {out_5, out_4};
  assign out_8 = {out_5[0], out_4};
  assign out_9 = {out_5, out_4, out_3, out_2};

  // Other names for the same wires on the sheet: Imm_11[10:0] = {out_5, out_4, out_3, out_2};
  //   Instruction[15:0] = {out_6, out_5, out_4, out_3, out_2}; Rt[2:0] = out_2; Rs[2:0] = out_3;
  //   Imm_5[4:0] = {out_5, out_4}; Rd[2:0] = out_4; Shift_amount[3:0] = {out_5[0], out_4}; F[1:0] = out_5;
  //   OP[4:0] = out_6
endmodule
